# Fritzing sketch schema (saved by Fritzing 1.0.2b)
breadboards: 1

parts:
  U1 = atmega328 [package=dip]
  LED2 = LED - 3mm [color="Red (633nm)" current=0.030 package="3 mm [THT]"]
  LED3 = LED - 3mm [color="Red (633nm)" current=0.030 package="3 mm [THT]"]
  LED4 = LED - 3mm [color="Yellow (595nm)" current=0.030 package="3 mm [THT]"]
  R2 = Resistor [tolerance=±5% resistance=470 power=0.25 package=THT]
  R3 = Resistor [tolerance=±5% resistance=470 power=0.25 package=THT]
  R4 = Resistor [tolerance=±5% resistance=470 power=0.25 package=THT]
  Mod1 = Passive Buzzer
  BAT1 = LIPO-110mAh [package=lipo-110]
  ISP = Header 5x2 [package=avr_icsp]
  RE1 = KY-040 Rotary encoder [package="Breakout board"]
  Mod2 = 2S-BMS
  XTAL1 = CRYSTAL - kHz [frequency="32 kHz"]

nets:
  N1: U1.RESET, ISP.5
  N2: U1.D2, RE1.CLK
  N3: U1.D3_(PWM), RE1.DT
  N4: U1.D4, RE1.SW
  VCC: U1.VCC, U1.AVCC, LED2.anode, LED3.anode, LED4.anode, ISP.2, RE1.Vcc, Mod2.pin3#3
  GND: U1.GND, ISP.4, ISP.6, ISP.8, ISP.10, RE1.GND, Mod2.pin3#2
  N5: U1.XLAT1, XTAL1.pin_0
  N6: U1.XLAT2, XTAL1.pin_1
  N7: U1.D9_(PWM), Mod1.S, Mod1.NC
  N8: U1.D10_(PWM), Mod1.-
  N9: U1.D11_(PWM), ISP.1
  N10: U1.D12, ISP.9
  N11: U1.D13, ISP.7
  N12: U1.A0, R2.Pin_0
  N13: U1.A1, R3.Pin_0
  N14: U1.A2, R4.Pin_0
  N15: LED2.cathode, R2.Pin_1
  N16: LED3.cathode, R3.Pin_1
  N17: LED4.cathode, R4.Pin_1
  N18: BAT1.+, Mod2.pin1
  N19: BAT1.-, Mod2.pin2

custom parts:
  KY-040 Rotary encoder: KY-040 Rotary Encoder with switch on breakout borad from AZ Delivery
  2S-BMS: 2S-BMS LIPO battery charger / protection unit. Note pcb does not match the board as it will likely connect with wires, so pcb is 5 pads suitable for .1in header pins.
